# Fritzing sketch final-project-design (saved by Fritzing 0.9.6b)
breadboards: 1

parts:
  Part1 = Arduino Uno (Rev3) - ICSP
  HC-SR04_Sensor_1 = HC-SR04 Ultrasonic Distance Sensor
  HC-SR04_Sensor_2 = HC-SR04 Ultrasonic Distance Sensor
  Part2 = LCD1602-I2C
  U1 = NodeMCU V1.0
  M1 = Osoyoo SX1278-ra-02
  M2 = Osoyoo SX1278-ra-02

nets:
  N1: Part1.D8, HC-SR04_Sensor_2.TRIG
  N2: Part1.A4/SDA, Part2.SDA
  N3: Part1.A5/SCL, Part2.SCL
  N4: Part1.D3_PWM, HC-SR04_Sensor_1.ECHO
  N5: Part1.D4, HC-SR04_Sensor_1.TRIG
  N6: Part1.D7, HC-SR04_Sensor_2.ECHO
  3V3: Part1.3V3, M1.3.3V
  GND: Part1.GND, HC-SR04_Sensor_1.GND, HC-SR04_Sensor_2.GND, Part2.GND, U1.GND, M1.GND, M2.GND
  VCC: Part1.VIN, HC-SR04_Sensor_1.VCC, HC-SR04_Sensor_2.VCC, Part2.VCC, U1.Vin
  N7: U1.D2, M2.DIO0
  3V3_2: U1.3V3, M2.3.3V

custom parts:
  LCD1602-I2C: A standard character display, usually with 2x16 characters. Comes in many colors with LCM1602 IIC attached.
  NodeMCU V1.0: ESP8266 based NodeMCU
  Osoyoo SX1278-ra-02: Osoyoo Long Distance wireless transceiver Uart LoRa Module.
